# Fritzing sketch Antilog-NPNO_TLF01_V2_0_RevA_Test (saved by Fritzing 0.9.4)
perfboards: 1

parts:
  R1 = Rotary Potentiometer (Small) [maximum_resistance=100kΩ package=THT]  # not connected
  R2 = Rotary Potentiometer (Small) [maximum_resistance=100kΩ package=THT]  # not connected
  J1 = female pin header, 3 pins [form="♀ (female)"]  # not connected
  J2 = female pin header, 2 pins [form="♀ (female)"]
  J3 = female pin header, 2 pins [form="♀ (female)"]  # not connected
  R3 = Resistor [tolerance=±5% resistance=1k package=THT]

nets:
  N1: J2.pin2, R3.Pin_1

notes:
  +/- 12V PSU
  +12V
  Antilog-NPNO
  for TLF01 V2.0 Rev.A
  I_SINK
  Cutoff
