# Fritzing sketch TLF01_V2_Test (saved by Fritzing 0.9.3b)
breadboards: 1
perfboards: 1

parts:
  Q1 = Basic FET P-Channel [package="TO220 [THT]"]
  R1 = Rotary Potentiometer (Small) [maximum_resistance=100kΩ package=THT]
  J1 = female pin header, 2 pins [form="♀ (female)"]
  R2 = Resistor [tolerance=±5% resistance=1k package=THT]

nets:
  N1: Q1.gate, R2.Pin_1
  N2: Q1.drain, Q1.source, R1.leg1, R1.wiper, R1.leg2, J1.pin1
  N3: J1.pin2, R2.Pin_0

notes:
  2SK170
  D / G / S
  TLF01 V2.0
  JFET
  Current Sink
